# Fritzing sketch vu_meter (saved by Fritzing 0.9.2b)
breadboards: 1

parts:
  Part1 = Arduino Uno (Rev3)
  LED1 = LED - 5mm [color="Red (633nm)" package="5 mm [THT]"]
  LED2 = LED - 5mm [color="Red (633nm)" package="5 mm [THT]"]
  LED3 = LED - 5mm [color="Red (633nm)" package="5 mm [THT]"]
  LED4 = LED - 5mm [color="Green (570nm)" package="5 mm [THT]"]
  LED5 = LED - 5mm [color="Green (570nm)" package="5 mm [THT]"]
  LED6 = LED - 5mm [color="Green (570nm)" package="5 mm [THT]"]
  LED7 = LED - 5mm [color="Green (570nm)" package="5 mm [THT]"]
  LED8 = LED - 5mm [color="Blue (525nm)" package="5 mm [THT]"]
  LED9 = LED - 5mm [color="Blue (525nm)" package="5 mm [THT]"]
  LED10 = LED - 5mm [color="Blue (525nm)" package="5 mm [THT]"]
  LED11 = LED - 5mm [color="White (4500K)" package="5 mm [THT]"]
  R1 = Resistor [tolerance=±5% resistance=100 package=THT]
  R2 = Resistor [tolerance=±5% resistance=100 package=THT]
  R3 = Resistor [tolerance=±5% resistance=100 package=THT]
  R4 = Resistor [tolerance=±5% resistance=100 package=THT]
  R5 = Resistor [tolerance=±5% resistance=100 package=THT]
  R6 = Resistor [tolerance=±5% resistance=100 package=THT]
  R7 = Resistor [tolerance=±5% resistance=100 package=THT]
  R8 = Resistor [tolerance=±5% resistance=100 package=THT]
  R9 = Resistor [tolerance=±5% resistance=100 package=THT]
  R10 = Resistor [tolerance=±5% resistance=100 package=THT]
  R11 = Resistor [tolerance=±5% resistance=100 package=THT]
  BAT1 = BC9VPC [package=bc9vpc]
  U2 = 3.5mm Audio Jack [package=audio-jack-3.5mm-smd]

nets:
  N1: Part1.A0, U2.RIGHT, U2.SLEEVE
  N2: Part1.D8, R3.Pin_1
  N3: Part1.D9_PWM, R2.Pin_1
  N4: Part1.D10_PWM/SS, R1.Pin_1
  N5: Part1.GND, LED1.cathode, LED2.cathode, LED3.cathode, LED4.cathode, LED5.cathode, LED6.cathode, LED7.cathode, LED8.cathode, LED9.cathode, LED10.cathode, LED11.cathode, BAT1.V-, U2.LEFT
  N6: Part1.D0/RX, R11.Pin_1
  N7: Part1.D1/TX, R10.Pin_1
  N8: Part1.D2, R9.Pin_1
  N9: Part1.D3_PWM, R8.Pin_1
  N10: Part1.D4, R7.Pin_1
  N11: Part1.D5_PWM, R6.Pin_1
  N12: Part1.D6_PWM, R5.Pin_1
  N13: Part1.D7, R4.Pin_1
  N14: Part1.VIN, BAT1.V+
  N15: LED1.anode, R1.Pin_0
  N16: LED2.anode, R2.Pin_0
  N17: LED3.anode, R3.Pin_0
  N18: LED4.anode, R4.Pin_0
  N19: LED5.anode, R5.Pin_0
  N20: LED6.anode, R6.Pin_0
  N21: LED7.anode, R7.Pin_0
  N22: LED8.anode, R8.Pin_0
  N23: LED9.anode, R9.Pin_0
  N24: LED10.anode, R10.Pin_0
  N25: LED11.anode, R11.Pin_0
